# Fritzing sketch schematic (saved by Fritzing 0.9.0b)
breadboards: 1

parts:
  Part1 = Arduino Uno (Rev3)
  INA1 = INA219 DC Current Sensor Breakout
  OLED1 = 128x32 I2C Monochrome OLED Display
  J1 = Power Jack [package=power_jack_pth]
  M1 = DC Motor

nets:
  GND: Part1.GND, INA1.GND, OLED1.GND, J1.GND, M1.pin_1
  N1: Part1.A4/SDA, INA1.SDA, OLED1.SDA
  N2: Part1.A5/SCL, INA1.SCL, OLED1.SCL
  N3: Part1.D4, OLED1.RST
  5V: Part1.5V, INA1.VCC
  N4: INA1.Vin+2, J1.PWR

custom parts:
  INA219 DC Current Sensor Breakout: INA DC Current Sensor Breakout
